// Logisim project circuit.circ as structural Verilog: 1 circuit, main circuit main
module main (
  input  X0,
  input  X1,
  input  X2,
  input  X1_2,
  input  X0_2,
  input  X2_2,
  output out_7,
  output out_8
);

  wire and_1_out, not_1_out, not_2_out, or_1_out, or_2_out;

  not not_1 (not_1_out, X2);
  not not_2 (not_2_out, X2_2);
  and and_1 (and_1_out, X1, not_1_out);
  or or_1 (or_1_out, X1_2, X0_2);
  or or_2 (or_2_out, X0_2, not_2_out);
  or or_3 (out_7, X0, and_1_out);
  and and_2 (out_8, or_1_out, or_2_out);
endmodule
