// Logisim project circuit-diagram.circ as structural Verilog: 1 circuit, main circuit main
module main (
  input  [2:0] x4x3x2,
  input  x1,
  input  x0,
  output out_4
);

  wire and_1_out, and_2_out, not_1_out, not_2_out, not_3_out;

  not not_1 (not_1_out, x0);
  not not_2 (not_2_out, x1);
  and and_1 (and_1_out, not_1_out, not_2_out);
  and and_2 (and_2_out, x1, x0);
  not not_3 (not_3_out, and_1_out);
  Multiplexer #(.select(3), .enable("false")) multiplexer_1 (
    .in0(x1), .in1(x0), .in2(not_1_out), .in3(not_1_out), .in4(and_2_out), .in5(not_3_out), .in6(and_1_out),
    .in7(and_2_out), .out(out_4), .sel(x4x3x2));
endmodule
