// Logisim project exp2-sketch.circ as structural Verilog: 1 circuit, main circuit main
module main (
  input  [2:0] x4_x3_x2,
  input  [1:0] x1_x0,
  output y
);

  wire decoder_1_out0, decoder_1_out3, not_1_out, not_2_out;

  not not_1 (not_1_out, x1_x0[0]);
  Decoder #(.select(2), .enable("false")) decoder_1 (
    .out0(decoder_1_out0), .out3(decoder_1_out3), .sel(x1_x0));  // open: out1, out2
  not not_2 (not_2_out, decoder_1_out0);
  Multiplexer #(.select(3), .enable("false")) multiplexer_1 (
    .in0(x1_x0[1]), .in1(x1_x0[0]), .in2(not_1_out), .in3(not_1_out), .in4(decoder_1_out3), .in5(not_2_out),
    .in6(decoder_1_out0), .in7(decoder_1_out3), .out(y), .sel(x4_x3_x2));

  // Notes on the sheet:
  //   x1 x0
endmodule
